// Logisim project s-mips.circ as structural Verilog: 23 circuits, main circuit S-MIPS Board
module S_MIPS (
  input  Kbd_Available,
  input  [6:0] Kbd_ASCII_Data,
  input  [31:0] RAM_Out_0,
  input  [31:0] RAM_Out_1,
  input  Reset,
  input  [31:0] RAM_Out_2,
  input  Clock,
  input  [31:0] RAM_Out_3,
  input  [3:0] Read_Time,
  input  [3:0] Write_Time,
  output Kbd_Enable,
  output [15:0] Address,
  output Kbd_Clear,
  output TTY_Enable,
  output [6:0] TTY_ASCII_Data,
  output Stop,
  output [31:0] RAM_In_0,
  output [31:0] RAM_In_1,
  output [31:0] RAM_In_2,
  output [31:0] RAM_In_3,
  output [3:0] Mask,
  output nRead_Write,
  output Chip_Select
);

  wire ALU_inst, d_ff_2_q, get_data, get_inst, GI_en, halt, jmp_inst, mem_inst, or_1_out, or_2_out, PC_en,
       R_inst, ready_data, ready_inst, ready_write, RF_en, stack_inst, start, tty, write, write_inst;
  wire [31:0] address_t, instruction, multiplexer_1_out, multiplexer_2_out, multiplexer_3_out,
       multiplexer_4_out, ram_interaction_1_output, ram_interaction_1_output_2, ram_interaction_1_output_3,
       ram_interaction_1_output_4;

  Multiplexer #(.width(32), .enable("false")) multiplexer_1 (
    .in0(RAM_Out_0), .in1(RAM_In_0), .out(multiplexer_1_out), .sel(write));
  Multiplexer #(.width(32), .enable("false")) multiplexer_2 (
    .in0(RAM_Out_1), .in1(RAM_In_0), .out(multiplexer_2_out), .sel(write));
  Multiplexer #(.width(32), .enable("false")) multiplexer_3 (
    .in0(RAM_Out_2), .in1(RAM_In_0), .out(multiplexer_3_out), .sel(write));
  Multiplexer #(.width(32), .enable("false")) multiplexer_4 (
    .in0(RAM_Out_3), .in1(RAM_In_0), .out(multiplexer_4_out), .sel(write));
  D_Flip_Flop #(.trigger("falling")) d_ff_1 (.clk(Clock), .D(Reset), .Q(start));  // open: Qn, preset, en, reset
  or or_1 (or_1_out, get_inst, ready_inst);
  RAM_Interaction ram_interaction_1 (
    .in_1(multiplexer_1_out), .in_2(multiplexer_2_out), .in_3(multiplexer_3_out), .in_4(multiplexer_4_out),
    .in_5(address_t), .in_6(Read_Time), .in_7(Write_Time), .in_9(Reset), .in_10(write), .in_11(get_inst),
    .in_12(get_data), .in_13(GI_en), .Output(ram_interaction_1_output),
    .Output_2(ram_interaction_1_output_2), .Output_3(ram_interaction_1_output_3),
    .Output_4(ram_interaction_1_output_4), .Output_5(Address), .Output_6(Mask), .Output_7(Chip_Select),
    .Output_8(nRead_Write), .Output_9(ready_inst), .Output_10(ready_data), .Output_11(ready_write),
    .in_8(Clock));
  D_Flip_Flop #(.trigger("falling")) d_ff_2 (
    .clk(Clock), .D(get_inst), .Q(d_ff_2_q), .en(or_1_out));  // open: Qn, preset, reset
  or or_2 (or_2_out, stack_inst, mem_inst);
  Control_Unit control_unit_1 (
    .in_2(start), .in_3(ready_inst), .in_4(ALU_inst), .in_5(R_inst), .in_6(Reset), .in_7(tty),
    .in_8(ready_data), .in_9(jmp_inst), .in_10(or_2_out), .in_11(write_inst), .in_12(ready_write),
    .Output(RF_en), .Output_2(PC_en), .Output_3(Stop), .Output_4(get_data), .Output_5(get_inst),
    .Output_6(GI_en), .Output_7(TTY_Enable), .Output_8(Kbd_Enable), .Output_9(write), .in_1(Clock));
  Data_Path data_path_1 (
    .in_2(Clock), .in_3(RF_en), .in_4(Reset), .in_5(Kbd_Available), .in_6(GI_en), .in_7(PC_en),
    .in_8(Kbd_ASCII_Data), .Output_10(TTY_ASCII_Data), .in_9(d_ff_2_q), .Output(halt), .Output_2(ALU_inst),
    .Output_3(R_inst), .Output_4(jmp_inst), .Output_5(address_t), .Output_6(tty), .Output_7(mem_inst),
    .Output_8(stack_inst), .Output_9(write_inst),
    .R_out({RAM_In_0[7:0], RAM_In_0[15:8], RAM_In_0[23:16], RAM_In_0[31:24]}), .in_1(instruction));
  Multiplexer #(.select(2), .width(32), .enable("false")) multiplexer_5 (
    .in0(ram_interaction_1_output), .in1(ram_interaction_1_output_2), .in2(ram_interaction_1_output_3),
    .in3(ram_interaction_1_output_4), .out(instruction), .sel(address_t[3:2]));

  assign Kbd_Clear = Reset;
  assign RAM_In_1 = RAM_In_0;
  assign RAM_In_2 = RAM_In_0;
  assign RAM_In_3 = RAM_In_0;

  // Other names for the same wires on the sheet: CLK = Clock; CS = Chip_Select; KBD_AVAIL = Kbd_Available;
  //   CLR = Reset; KBD_CLR = Reset; KBD_DATA[6:0] = Kbd_ASCII_Data; R_out[31:0] = RAM_In_0;
  //   RAM_INPUT_0[31:0] = RAM_In_0; RAM_INPUT_1[31:0] = RAM_In_0; RAM_INPUT_2[31:0] = RAM_In_0;
  //   RAM_INPUT_3[31:0] = RAM_In_0; RAM_A[15:0] = Address; RAM_MASK[3:0] = Mask; RAM_OUTPUT_0[31:0] = RAM_Out_0;
  //   RAM_OUTPUT_1[31:0] = RAM_Out_1; RAM_OUTPUT_2[31:0] = RAM_Out_2; RAM_OUTPUT_3[31:0] = RAM_Out_3;
  //   RW = nRead_Write; TTY_DATA[6:0] = TTY_ASCII_Data

  // Notes on the sheet:
  //   RAM ADDRESS
  //   DATA FROM RAM
  //   DATA TO RAM
  //   DATA WRITE MASK
  //   RAM TIMING
  //   RAM CONTROL
  //   KEYBOARD
  //   TTY
  //   SEQUENCING
  //   S-MIPS
  //   CPU
endmodule

module S_MIPS_Board (
  input  DESHABILITAR_DISPATCHER,
  output halt
);

  wire button_1_out, CLK, CS, d_ff_1_q, LCLR, LoadRAM, LoadRAMOn, LW, R_R_W, R_W, ram_dispatcher_1_finished,
       RCS, Reset_out, RST, TTY_EN;
  wire [2:0] KDB;
  wire [3:0] LMask, Mask, ram_1_read_time, ram_1_write_time, RMask;
  wire [6:0] KDB_DATA, TTY_DATA;
  wire [15:0] Addr, LAddr, RAddr;
  wire [31:0] I0, I1, I2, I3, LData, ram_1_data_out_0, ram_1_data_out_1, ram_1_data_out_2, ram_1_data_out_3,
       RI0, RI1, RI2, RI3;

  TTY #(.rows(25), .cols(80)) tty_1 (.data(TTY_DATA), .clk(CLK), .we(TTY_EN), .clr(RST));
  not not_1 (LoadRAMOn, ram_dispatcher_1_finished);
  RAM_Dispatcher ram_dispatcher_1 (
    .WriteTime(ram_1_write_time), .Clock(CLK), .Data(LData), .Address(LAddr), .Mask(LMask),
    .Finished(ram_dispatcher_1_finished), .Write(LW), .CLR(LCLR));
  Keyboard #(.buflen(64)) keyboard_1 (.clk(CLK), .re(KDB[0]), .avail(KDB[2]), .data(KDB_DATA));  // open: clr
  RAM ram_1 (
    .Address(RAddr), .Data_Out_0(ram_1_data_out_0), .Data_Out_1(ram_1_data_out_1),
    .Data_Out_2(ram_1_data_out_2), .Data_Out_3(ram_1_data_out_3), .Data_In_0(RI0), .Data_In_1(RI1),
    .Data_In_2(RI2), .Data_In_3(RI3), .Mask(RMask), .nRead_Write(R_R_W), .Chip_Select(RCS),
    .Read_Time(ram_1_read_time), .Reset(button_1_out), .Write_Time(ram_1_write_time));
  Button button_1 (.out(button_1_out));
  D_Flip_Flop d_ff_1 (.clk(CLK), .D(1'b1), .Q(d_ff_1_q), .reset(Reset_out));  // open: Qn, preset, en
  Button Reset (.out(Reset_out));
  S_MIPS s_mips_1 (
    .Kbd_Enable(KDB[0]), .Address(Addr), .Kbd_Clear(KDB[1]), .Kbd_Available(KDB[2]), .RAM_In_0(I0),
    .Kbd_ASCII_Data(KDB_DATA), .RAM_In_1(I1), .TTY_Enable(TTY_EN), .RAM_In_2(I2), .RAM_In_3(I3),
    .TTY_ASCII_Data(TTY_DATA), .Reset(RST), .RAM_Out_0(ram_1_data_out_0), .Clock(CLK),
    .RAM_Out_1(ram_1_data_out_1), .Stop(halt), .RAM_Out_2(ram_1_data_out_2), .RAM_Out_3(ram_1_data_out_3),
    .Mask(Mask), .Read_Time(ram_1_read_time), .Write_Time(ram_1_write_time), .nRead_Write(R_W),
    .Chip_Select(CS));
  D_Flip_Flop d_ff_2 (.clk(CLK), .D(d_ff_1_q), .Qn(LCLR), .reset(Reset_out));  // open: Q, preset, en
  or or_1 (RST, LCLR, LoadRAM);
  Clock clock_1 (.out(CLK));
  Multiplexer #(.width(32), .enable("false")) multiplexer_1 (.in0(I0), .in1(LData), .out(RI0), .sel(LoadRAM));
  Multiplexer #(.width(32), .enable("false")) multiplexer_2 (.in0(I1), .in1(LData), .out(RI1), .sel(LoadRAM));
  Multiplexer #(.width(32), .enable("false")) multiplexer_3 (.in0(I2), .in1(LData), .out(RI2), .sel(LoadRAM));
  Multiplexer #(.width(32), .enable("false")) multiplexer_4 (.in0(I3), .in1(LData), .out(RI3), .sel(LoadRAM));
  and and_1 (LoadRAM, ~DESHABILITAR_DISPATCHER, LoadRAMOn);  // AND_Gate
  Multiplexer #(.width(16), .enable("false")) multiplexer_5 (.in0(Addr), .in1(LAddr), .out(RAddr), .sel(LoadRAM));
  Multiplexer #(.width(4), .enable("false")) multiplexer_6 (.in0(Mask), .in1(LMask), .out(RMask), .sel(LoadRAM));
  Multiplexer #(.enable("false")) multiplexer_7 (.in0(CS), .in1(LW), .out(RCS), .sel(LoadRAM));
  Multiplexer #(.enable("false")) multiplexer_8 (.in0(R_W), .in1(LW), .out(R_R_W), .sel(LoadRAM));

  // Notes on the sheet:
  //   NO MODIFICAR
  //   Keyboard
endmodule

module RAM (
  input  [15:0] Address,
  input  [31:0] Data_In_0,
  input  [31:0] Data_In_1,
  input  [31:0] Data_In_2,
  input  [31:0] Data_In_3,
  input  [3:0] Mask,
  input  nRead_Write,
  input  Chip_Select,
  input  Reset,
  output [31:0] Data_Out_0,
  output [31:0] Data_Out_1,
  output [31:0] Data_Out_2,
  output [31:0] Data_Out_3,
  output [3:0] Read_Time,
  output [3:0] Write_Time
);

  wire and_2_out, and_3_out, and_4_out, and_5_out, and_6_out, and_7_out, and_8_out, and_9_out, Changed, CLK,
       comparator_2_eq, comparator_3_eq, comparator_4_eq, comparator_5_eq, comparator_6_eq, Count,
       demultiplexer_3_out0, Idle, Idle_q, Load, Load0, Load1, nand_1_out, or_1_out, or_2_out, or_3_out,
       or_4_out, or_5_out, or_6_out, or_7_out, or_8_out, or_9_out, or_10_out, Proc_q, Update_Mem, Zero_Time;
  wire [3:0] counter_1_q, multiplexer_1_out, subtractor_1_out;
  wire [31:0] register_1_q, register_2_q, register_3_q, register_4_q, register_5_q;

  // Probe on 4'b0011
  // Probe on 4'b0010
  Multiplexer #(.width(4), .enable("false")) multiplexer_1 (
    .in0(4'b0011), .in1(4'b0010), .out(multiplexer_1_out), .sel(nRead_Write));
  or or_1 (or_1_out, Idle, Update_Mem);
  or or_2 (or_2_out, ~Chip_Select, Reset);  // OR_Gate
  Subtractor #(.width(4)) subtractor_1 (.a(multiplexer_1_out), .b(4'b0010), .out(subtractor_1_out));  // open: bin, bout
  D_Flip_Flop u_Idle (.clk(CLK), .D(or_1_out), .Q(Idle_q), .preset(or_2_out));  // open: Qn, en, reset
  Demultiplexer #(.enable("false")) demultiplexer_1 (.out0(Idle), .out1(Load0), .in(Idle_q), .sel(Changed));
  // Probe on counter_1_q
  Counter #(.width(4), .max('hf)) counter_1 (
    .load(Load), .D(subtractor_1_out), .count(Count), .Q(counter_1_q), .clk(CLK), .clr(or_3_out));  // open: carry
  or or_3 (or_3_out, ~Chip_Select, Reset);  // OR_Gate
  Comparator_part #(.width(4), .mode("unsigned")) comparator_1 (
    .a(4'b0000), .b(counter_1_q), .eq(Zero_Time));  // open: gt, lt
  or or_4 (or_4_out, Count, Load0, Load1);
  Register #(.width(32)) register_1 (.D(Data_In_0), .en(Chip_Select), .Q(register_1_q), .clk(CLK), .clr(or_5_out));
  or or_5 (or_5_out, ~Chip_Select, Reset);  // OR_Gate
  Register #(.width(32)) register_2 (.D(Data_In_1), .en(Chip_Select), .Q(register_2_q), .clk(CLK), .clr(or_6_out));
  or or_6 (or_6_out, ~Chip_Select, Reset);  // OR_Gate
  Register #(.width(32)) register_3 (.D(Data_In_2), .en(Chip_Select), .Q(register_3_q), .clk(CLK), .clr(or_7_out));
  or or_7 (or_7_out, ~Chip_Select, Reset);  // OR_Gate
  Register #(.width(32)) register_4 (.D(Data_In_3), .en(Chip_Select), .Q(register_4_q), .clk(CLK), .clr(or_8_out));
  or or_8 (or_8_out, ~Chip_Select, Reset);  // OR_Gate
  Register #(.width(32)) register_5 (
    .D({{11{1'b1}}, nRead_Write, Mask, Address}), .en(Chip_Select), .Q(register_5_q), .clk(CLK),
    .clr(or_9_out));
  or or_9 (or_9_out, ~Chip_Select, Reset);  // OR_Gate
  D_Flip_Flop Proc (.clk(CLK), .D(or_4_out), .Q(Proc_q), .reset(or_10_out));  // open: Qn, preset, en
  or or_10 (or_10_out, ~Chip_Select, Reset);  // OR_Gate
  Demultiplexer #(.enable("false")) demultiplexer_2 (
    .out0(Count), .out1(Update_Mem), .in(demultiplexer_3_out0), .sel(Zero_Time));
  Demultiplexer #(.enable("false")) demultiplexer_3 (
    .out0(demultiplexer_3_out0), .out1(Load1), .in(Proc_q), .sel(Changed));
  Clock clock_1 (.out(CLK));
  Comparator_part #(.width(32)) comparator_2 (.a(register_1_q), .b(Data_In_0), .eq(comparator_2_eq));  // open: gt, lt
  Comparator_part #(.width(32)) comparator_3 (.a(register_2_q), .b(Data_In_1), .eq(comparator_3_eq));  // open: gt, lt
  Comparator_part #(.width(32)) comparator_4 (.a(register_3_q), .b(Data_In_2), .eq(comparator_4_eq));  // open: gt, lt
  Comparator_part #(.width(32)) comparator_5 (.a(register_4_q), .b(Data_In_3), .eq(comparator_5_eq));  // open: gt, lt
  Comparator_part #(.width(32)) comparator_6 (
    .a(register_5_q), .b({{11{1'b1}}, nRead_Write, Mask, Address}), .eq(comparator_6_eq));  // open: gt, lt
  nand nand_1 (nand_1_out, comparator_6_eq, comparator_2_eq, comparator_3_eq, comparator_4_eq, comparator_5_eq);
  and and_1 (Changed, nand_1_out, Chip_Select);
  or or_11 (Load, Count, Load1, Load0);
  and and_2 (and_2_out, Mask[0], Update_Mem, nRead_Write);
  and and_3 (and_3_out, Mask[1], Update_Mem, nRead_Write);
  and and_4 (and_4_out, Mask[2], Update_Mem, nRead_Write);
  and and_5 (and_5_out, Mask[3], Update_Mem, nRead_Write);
  RAM_part #(.addrWidth(16), .dataWidth(32), .bus("separate")) ram_1 (
    .addr(Address), .din(Data_In_0), .data(Data_Out_0), .str(and_2_out), .sel(Chip_Select), .clk(CLK),
    .ld(and_6_out), .clr(Reset));
  and and_6 (and_6_out, ~nRead_Write, Idle);  // AND_Gate
  RAM_part #(.addrWidth(16), .dataWidth(32), .bus("separate")) ram_2 (
    .addr(Address), .din(Data_In_1), .data(Data_Out_1), .str(and_3_out), .sel(Chip_Select), .clk(CLK),
    .ld(and_7_out), .clr(Reset));
  and and_7 (and_7_out, ~nRead_Write, Idle);  // AND_Gate
  RAM_part #(.addrWidth(16), .dataWidth(32), .bus("separate")) ram_3 (
    .addr(Address), .din(Data_In_2), .data(Data_Out_2), .str(and_4_out), .sel(Chip_Select), .clk(CLK),
    .ld(and_8_out), .clr(Reset));
  and and_8 (and_8_out, ~nRead_Write, Idle);  // AND_Gate
  RAM_part #(.addrWidth(16), .dataWidth(32), .bus("separate")) ram_4 (
    .addr(Address), .din(Data_In_3), .data(Data_Out_3), .str(and_5_out), .sel(Chip_Select), .clk(CLK),
    .ld(and_9_out), .clr(Reset));
  and and_9 (and_9_out, ~nRead_Write, Idle);  // AND_Gate

  assign Read_Time = 4'b0011;
  assign Write_Time = 4'b0010;

  // Other names for the same wires on the sheet: M0 = Mask[0]; M1 = Mask[1]; M2 = Mask[2]; M3 = Mask[3];
  //   RW = nRead_Write; CLR = Reset; CS = Chip_Select; Load2 = Count

  // Notes on the sheet:
  //   NO MODIFICAR
  //   excepto quizás los valores RT y WT
  //   BANK0
  //   BANK1
  //   BANK2
  //   BANK3
endmodule

module RAM_Dispatcher (
  input  [3:0] WriteTime,
  input  Clock,
  input  CLR,
  output [31:0] Data,
  output [15:0] Address,
  output [3:0] Mask,
  output Finished,
  output Write
);

  wire demultiplexer_2_out1, demultiplexer_3_out1, End, IDLE_q, IncAddr, Load, or_1_out, or_2_out, While_q,
       WriteEnd;
  wire [3:0] counter_1_q;
  wire [31:0] CurrentAddress_q;

  Counter #(.width(32), .max('hffffffff)) CurrentAddress (
    .count(IncAddr), .Q({CurrentAddress_q[31:18], Address, CurrentAddress_q[1:0]}), .clk(Clock), .clr(CLR));  // open: load, D, carry
  or or_1 (or_1_out, IncAddr, demultiplexer_3_out1, Finished);
  D_Flip_Flop IDLE (.clk(Clock), .D(or_1_out), .Q(IDLE_q), .preset(CLR));  // open: Qn, en, reset
  Demultiplexer #(.enable("false")) demultiplexer_1 (.out0(Load), .out1(Finished), .in(IDLE_q), .sel(End));
  D_Flip_Flop While (.clk(Clock), .D(or_2_out), .Q(While_q), .reset(CLR));  // open: Qn, preset, en
  or or_2 (or_2_out, Write, Load);
  RAM_part #(.addrWidth(18), .dataWidth(32)) ram_1 (
    .addr({Address, CurrentAddress_q[1:0]}), .data(Data), .clk(Clock));  // open: sel, ld, clr
  Demultiplexer #(.enable("false")) demultiplexer_2 (
    .out0(Write), .out1(demultiplexer_2_out1), .in(While_q), .sel(WriteEnd));
  Decoder #(.select(2)) decoder_1 (
    .out0(Mask[0]), .out1(Mask[1]), .out2(Mask[2]), .out3(Mask[3]), .sel(CurrentAddress_q[1:0]));  // open: en
  Demultiplexer #(.enable("false")) demultiplexer_3 (
    .out0(IncAddr), .out1(demultiplexer_3_out1), .in(demultiplexer_2_out1), .sel(End));
  Counter #(.width(4), .max('hf)) counter_1 (
    .load(Load), .D(WriteTime), .count(Write), .Q(counter_1_q), .clk(Clock));  // open: carry, clr
  Comparator_part #(.width(32)) comparator_1 (.a(Data), .b({32{1'b1}}), .eq(End));  // open: gt, lt
  Comparator_part #(.width(4)) comparator_2 (.a(4'b0000), .b(counter_1_q), .eq(WriteEnd));  // open: gt, lt

  // Other names for the same wires on the sheet: CLK = Clock; Count = Write; WT[3:0] = WriteTime
endmodule

module Data_Path (
  input  [31:0] in_1,
  input  in_2,
  input  in_3,
  input  in_4,
  input  in_5,
  input  in_6,
  input  in_7,
  input  [6:0] in_8,
  input  in_9,
  output Output,
  output Output_2,
  output Output_3,
  output Output_4,
  output [31:0] Output_5,
  output Output_6,
  output Output_7,
  output Output_8,
  output Output_9,
  output [6:0] Output_10,
  output [31:0] R_out
);

  wire ADD, add_t, addi, AND, and_t, andi, beq, bgtz, blez, bltz, bne, DIV, div_t, divu, I, j, jr, kbd, lw,
       mfhi, mflo, MUL, mult, mulu, nop, \nor , OR, or_10_out, or_t, ori, pop, push, rnd, sign, SLT, slt_t,
       SLTI, slti_t, sltiu, sltu, sub, sw, XOR, xor_t, xori;
  wire [3:0] ALU_selector;
  wire [4:0] multiplexer_2_out, RD, RS, RT;
  wire [15:0] \const ;
  wire [25:0] dest;
  wire [31:0] ALUout, HI, instruction_catcher_1_output, LO, multiplexer_1_out, PCin, PCout, random_1_out,
       register_file_input_1_output, RT_t, SP;
  wire [31:7] RS_t;
  wire [31:31] and_1_out;

  Instruction_Catcher instruction_catcher_1 (
    .in_4(in_1), .Output(instruction_catcher_1_output), .in_1(in_2), .in_2(in_4), .in_3(in_6));
  // Probe on RS
  // Probe on RT
  or or_1 (MUL, mult, mulu);
  or or_2 (DIV, div_t, divu);
  or or_3 (SLT, slt_t, sltu);
  or or_4 (SLTI, slti_t, sltiu);
  // Probe on RD
  or or_5 (Output_2, MUL, DIV, SLT, SLTI, AND, OR, XOR, ADD, \nor , sub);
  Instruction_Decoder instruction_decoder_1 (
    .Output(RS), .Output_2(dest), .in_1(instruction_catcher_1_output), .Output_3(RT), .Output_4(j),
    .Output_5(\const ), .Output_6(RD), .Output_7(nop), .Output_8(slt_t), .Output_9(addi), .Output_10(sw),
    .Output_11(add_t), .Output_12(sltu), .Output_13(slti_t), .Output_14(beq), .Output_15(sub),
    .Output_16(and_t), .Output_17(sltiu), .Output_18(bne), .Output_19(mult), .Output_20(or_t),
    .Output_21(andi), .Output_22(blez), .Output_23(mulu), .Output_24(\nor ), .Output_25(ori),
    .Output_26(bgtz), .Output_27(div_t), .Output_28(xor_t), .Output_29(xori), .Output_30(bltz),
    .Output_31(divu), .Output_32(lw), .Output_33(pop), .Output_34(Output), .Output_35(push),
    .Output_36(Output_6), .Output_37(jr), .Output_38(rnd), .Output_39(mfhi), .Output_40(kbd), .Output_41(mflo));
  or or_6 (AND, and_t, andi);
  or or_7 (OR, or_t, ori);
  or or_8 (XOR, xor_t, xori);
  or or_9 (ADD, add_t, addi);
  or or_10 (or_10_out, sw, addi, lw);
  ALU_Encoder alu_encoder_1 (
    .in_1(add_t), .in_2(sub), .in_3(mult), .in_4(mulu), .in_5(div_t), .in_6(divu), .in_7(slt_t), .in_8(sltu),
    .in_9(and_t), .in_10(or_t), .in_11(\nor ), .in_12(xor_t), .in_13(or_10_out), .in_14(slti_t),
    .in_15(sltiu), .in_16(andi), .in_17(ori), .in_18(xori), .sign(sign), .I(I), .selector(ALU_selector));
  and and_1 (and_1_out[31], \const [15], ~ori, ~andi, ~xori);  // AND_Gate
  Random #(.width(32)) random_1 (.clk(in_2), .next(rnd), .out(random_1_out));  // open: clr
  Multiplexer #(.width(32), .enable("false")) multiplexer_1 (
    .in0(RT_t), .in1({{16{and_1_out[31]}}, \const }), .out(multiplexer_1_out), .sel(I));
  Memory_Address memory_address_1 (
    .in_1(PCout), .in_2(ALUout), .in_3(SP), .in_4(lw), .in_6(pop), .in_8(in_9), .in_5(sw), .in_7(push),
    .Output(Output_5));
  ALU alu_1 (
    .in_1(sign), .Input({RS_t, Output_10}), .Input_2(multiplexer_1_out), .in_5(ALU_selector),
    .Output(ALUout), .Output_2(LO), .Output_3(HI), .in_2(in_2));
  or or_11 (Output_4, beq, bltz, bne, bgtz, blez, j, jr, nop);
  or or_12 (Output_3, rnd, mflo, kbd, mfhi, Output_6);
  Register_File_Input register_file_input_1 (
    .in_1(in_8), .in_2(ALUout), .in_3(lw), .in_5(random_1_out), .in_4(pop), .in_6(mfhi), .in_8(in_1),
    .in_7(mflo), .in_9(rnd), .in_10(kbd), .in_11(HI), .in_12(LO), .Output(register_file_input_1_output));
  Multiplexer #(.width(5), .enable("false")) multiplexer_2 (.in0(RD), .in1(RT), .out(multiplexer_2_out), .sel(I));
  Program_Counter program_counter_1 (.in_1(in_2), .Input(PCin), .in_2(in_7), .in_3(in_4), .Output(PCout));
  Branch_Control branch_control_1 (
    .in_1(dest), .in_2({RS_t, Output_10}), .in_3(RT_t), .in_4(PCout), .in_5(\const ), .in_6(beq), .in_7(bne),
    .in_8(blez), .in_9(bgtz), .in_10(bltz), .in_11(jr), .in_12(j), .Output(PCin));
  or or_13 (Output_7, sw, lw);
  or or_14 (Output_8, pop, push);
  or or_15 (Output_9, sw, push);
  Multiplexer #(.width(32), .enable("false")) multiplexer_3 (
    .in0({RS_t, Output_10}), .in1(RT_t), .out(R_out), .sel(sw));
  Register_File register_file_1 (
    .in_1(in_4), .in_2(in_3), .in_3(push), .in_4(register_file_input_1_output), .in_5(in_2), .in_6(in_7),
    .in_7(pop), .in_8(multiplexer_2_out), .in_9(RS), .in_10(RT), .Output({RS_t, Output_10}), .Output_2(RT_t),
    .Output_3(SP));

  // Other names for the same wires on the sheet: address[31:0] = Output_5; ALU_inst = Output_2; clock = in_2;
  //   enGI = in_6; enPC = in_7; enRF = in_3; halt = Output; instruction[31:0] = in_1; jmp_inst = Output_4;
  //   KBDava = in_5; KBDdata[6:0] = in_8; mem_inst = Output_7; nexti = in_9; R_inst = Output_3; reset = in_4;
  //   RS_t[6:0] = Output_10; tty_data[6:0] = Output_10; stack_inst = Output_8; tty = Output_6; write_inst = Output_9
endmodule

module Control_Unit (
  input  in_1,
  input  in_2,
  input  in_3,
  input  in_4,
  input  in_5,
  input  in_6,
  input  in_7,
  input  in_8,
  input  in_9,
  input  in_10,
  input  in_11,
  input  in_12,
  output Output,
  output Output_2,
  output Output_3,
  output Output_4,
  output Output_5,
  output Output_6,
  output Output_7,
  output Output_8,
  output Output_9
);

  wire branch, d_ff_1_q, d_ff_2_q, d_ff_3_q, d_ff_4_q, demultiplexer_1_out0, demultiplexer_1_out1, or_5_out,
       RF;
  wire [2:0] or_4_out;

  D_Flip_Flop #(.trigger("falling")) d_ff_1 (.clk(in_1), .D(in_2), .Q(d_ff_1_q), .reset(in_6));  // open: Qn, preset, en
  or or_1 (or_4_out[2], in_10, in_11);
  D_Flip_Flop #(.trigger("falling")) d_ff_2 (.clk(in_1), .D(in_3), .Q(d_ff_2_q));  // open: Qn, preset, en, reset
  Demultiplexer #(.select(3), .enable("false")) demultiplexer_1 (
    .out0(demultiplexer_1_out0), .out1(demultiplexer_1_out1), .out2(branch), .out3(RF), .out4(Output_4),
    .out5(Output_9), .in(d_ff_2_q), .sel(or_4_out));  // open: out6, out7
  or or_2 (or_4_out[1], in_5, in_9);
  D_Flip_Flop #(.trigger("falling")) d_ff_3 (
    .clk(in_1), .D(Output_2), .Q(d_ff_3_q), .reset(in_6));  // open: Qn, preset, en
  or or_3 (Output_5, d_ff_1_q, d_ff_3_q);
  or or_4 (or_4_out[0], in_5, in_4, in_11);
  or or_5 (or_5_out, Output_3, demultiplexer_1_out0);
  D_Flip_Flop #(.trigger("falling")) d_ff_4 (
    .clk(in_1), .D(demultiplexer_1_out1), .Q(d_ff_4_q), .reset(in_6));  // open: Qn, preset, en
  D_Flip_Flop #(.trigger("falling")) d_ff_5 (
    .clk(in_1), .D(or_5_out), .Q(Output_3), .reset(in_6));  // open: Qn, preset, en
  or or_6 (Output, d_ff_4_q, in_8, RF);
  D_Flip_Flop #(.trigger("falling")) d_ff_6 (.clk(in_1), .D(Output), .Q(Output_8));  // open: Qn, preset, en, reset
  and and_1 (Output_7, Output_8, in_7);
  or or_7 (Output_2, Output_8, in_12, branch);

  assign Output_6 = in_3;

  // Other names for the same wires on the sheet: ALU_inst = in_4; clock = in_1; cont = Output_2; PC_enable = Output_2;
  //   end = Output_3; get_data = Output_4; get_inst = Output_5; jmp_inst = in_9; mem_inst = in_10; R_inst = in_5;
  //   ready_data = in_8; GI_enable = in_3; ready_inst = in_3; ready_w = in_12; reset = in_6; RF_enable = Output;
  //   start = in_2; kbd_enable = Output_8; tty = Output_8; tty_enable = Output_7; tty_inst = in_7; write = Output_9;
  //   write_inst = in_11

  // Notes on the sheet:
  //   CONTROL UNIT
endmodule

module Instruction_Decoder (
  input  [31:0] in_1,
  output [4:0] Output,
  output [25:0] Output_2,
  output [4:0] Output_3,
  output Output_4,
  output [15:0] Output_5,
  output [4:0] Output_6,
  output Output_7,
  output Output_8,
  output Output_9,
  output Output_10,
  output Output_11,
  output Output_12,
  output Output_13,
  output Output_14,
  output Output_15,
  output Output_16,
  output Output_17,
  output Output_18,
  output Output_19,
  output Output_20,
  output Output_21,
  output Output_22,
  output Output_23,
  output Output_24,
  output Output_25,
  output Output_26,
  output Output_27,
  output Output_28,
  output Output_29,
  output Output_30,
  output Output_31,
  output Output_32,
  output Output_33,
  output Output_34,
  output Output_35,
  output Output_36,
  output Output_37,
  output Output_38,
  output Output_39,
  output Output_40,
  output Output_41
);

  wire _000000, _111111, comparator_14_eq, comparator_15_eq, comparator_16_eq, comparator_17_eq,
       comparator_18_eq, comparator_19_eq, comparator_20_eq, comparator_21_eq, comparator_22_eq,
       comparator_25_eq, comparator_26_eq, comparator_27_eq, comparator_28_eq, comparator_29_eq,
       comparator_30_eq, comparator_31_eq, comparator_32_eq, comparator_34_eq, comparator_35_eq,
       comparator_36_eq, comparator_37_eq, comparator_38_eq, comparator_39_eq, comparator_40_eq;

  Comparator_part #(.width(6)) comparator_1 (.a(in_1[31:26]), .b(6'b001000), .eq(Output_9));  // open: gt, lt
  Comparator_part #(.width(6)) comparator_2 (.a(in_1[31:26]), .b(6'b001010), .eq(Output_13));  // open: gt, lt
  Comparator_part #(.width(6)) comparator_3 (.a(in_1[31:26]), .b(6'b001011), .eq(Output_17));  // open: gt, lt
  Comparator_part #(.width(6)) comparator_4 (.a(in_1[31:26]), .b(6'b001100), .eq(Output_21));  // open: gt, lt
  Comparator_part #(.width(6)) comparator_5 (.a(in_1[31:26]), .b(6'b001101), .eq(Output_25));  // open: gt, lt
  Comparator_part #(.width(6)) comparator_6 (.a(in_1[31:26]), .b(6'b001110), .eq(Output_29));  // open: gt, lt
  Comparator_part #(.width(6)) comparator_7 (.a(in_1[31:26]), .b(6'b100011), .eq(Output_32));  // open: gt, lt
  Comparator_part #(.width(6)) comparator_8 (.a(in_1[31:26]), .b(6'b101011), .eq(Output_10));  // open: gt, lt
  Comparator_part #(.width(6)) comparator_9 (.a(in_1[31:26]), .b(6'b000100), .eq(Output_14));  // open: gt, lt
  Comparator_part #(.width(6)) comparator_10 (.a(in_1[31:26]), .b(6'b000101), .eq(Output_18));  // open: gt, lt
  Comparator_part #(.width(6)) comparator_11 (.a(in_1[31:26]), .b(6'b000110), .eq(Output_22));  // open: gt, lt
  Comparator_part #(.width(6)) comparator_12 (.a(in_1[31:26]), .b(6'b000111), .eq(Output_26));  // open: gt, lt
  Comparator_part #(.width(6)) comparator_13 (.a(in_1[31:26]), .b(6'b000001), .eq(Output_30));  // open: gt, lt
  Comparator_part #(.width(6)) comparator_14 (.a(in_1[5:0]), .b({6{1'b0}}), .eq(comparator_14_eq));  // open: gt, lt
  Comparator_part #(.width(6)) comparator_15 (.a(in_1[5:0]), .b(6'b100000), .eq(comparator_15_eq));  // open: gt, lt
  Comparator_part #(.width(6)) comparator_16 (.a(in_1[5:0]), .b(6'b100010), .eq(comparator_16_eq));  // open: gt, lt
  Comparator_part #(.width(6)) comparator_17 (.a(in_1[5:0]), .b(6'b011000), .eq(comparator_17_eq));  // open: gt, lt
  Comparator_part #(.width(6)) comparator_18 (.a(in_1[5:0]), .b(6'b011001), .eq(comparator_18_eq));  // open: gt, lt
  Comparator_part #(.width(6)) comparator_19 (.a(in_1[5:0]), .b(6'b011010), .eq(comparator_19_eq));  // open: gt, lt
  Comparator_part #(.width(6)) comparator_20 (.a(in_1[5:0]), .b(6'b011011), .eq(comparator_20_eq));  // open: gt, lt
  Comparator_part #(.width(6)) comparator_21 (.a(in_1[5:0]), .b(6'b000001), .eq(comparator_21_eq));  // open: gt, lt
  Comparator_part #(.width(6)) comparator_22 (.a(in_1[5:0]), .b(6'b000010), .eq(comparator_22_eq));  // open: gt, lt
  and and_1 (Output_7, _000000, comparator_14_eq);
  and and_2 (Output_11, _000000, comparator_15_eq);
  and and_3 (Output_15, _000000, comparator_16_eq);
  and and_4 (Output_19, _000000, comparator_17_eq);
  and and_5 (Output_23, _000000, comparator_18_eq);
  and and_6 (Output_27, _000000, comparator_19_eq);
  and and_7 (Output_31, _000000, comparator_20_eq);
  and and_8 (Output_36, _111111, comparator_21_eq);
  and and_9 (Output_38, _111111, comparator_22_eq);
  Comparator_part #(.width(6)) comparator_23 (.a(in_1[31:26]), .b({6{1'b1}}), .eq(_111111));  // open: gt, lt
  Comparator_part #(.width(6)) comparator_24 (.a(in_1[31:26]), .b({6{1'b0}}), .eq(_000000));  // open: gt, lt
  Comparator_part #(.width(6)) comparator_25 (.a(in_1[5:0]), .b(6'b101010), .eq(comparator_25_eq));  // open: gt, lt
  Comparator_part #(.width(6)) comparator_26 (.a(in_1[5:0]), .b(6'b101011), .eq(comparator_26_eq));  // open: gt, lt
  Comparator_part #(.width(6)) comparator_27 (.a(in_1[5:0]), .b(6'b100100), .eq(comparator_27_eq));  // open: gt, lt
  Comparator_part #(.width(6)) comparator_28 (.a(in_1[5:0]), .b(6'b100101), .eq(comparator_28_eq));  // open: gt, lt
  Comparator_part #(.width(6)) comparator_29 (.a(in_1[5:0]), .b(6'b100111), .eq(comparator_29_eq));  // open: gt, lt
  Comparator_part #(.width(6)) comparator_30 (.a(in_1[5:0]), .b(6'b101000), .eq(comparator_30_eq));  // open: gt, lt
  Comparator_part #(.width(6)) comparator_31 (.a(in_1[5:0]), .b(6'b000100), .eq(comparator_31_eq));  // open: gt, lt
  Comparator_part #(.width(6)) comparator_32 (.a(in_1[5:0]), .b({6{1'b1}}), .eq(comparator_32_eq));  // open: gt, lt
  and and_10 (Output_8, _000000, comparator_25_eq);
  and and_11 (Output_12, _000000, comparator_26_eq);
  and and_12 (Output_16, _000000, comparator_27_eq);
  and and_13 (Output_20, _000000, comparator_28_eq);
  and and_14 (Output_24, _000000, comparator_29_eq);
  and and_15 (Output_28, _000000, comparator_30_eq);
  and and_16 (Output_40, _111111, comparator_31_eq);
  and and_17 (Output_34, _111111, comparator_32_eq);
  Comparator_part #(.width(6)) comparator_33 (.a(in_1[31:26]), .b(6'b000010), .eq(Output_4));  // open: gt, lt
  Comparator_part #(.width(6)) comparator_34 (.a(in_1[31:26]), .b(6'b111000), .eq(comparator_34_eq));  // open: gt, lt
  Comparator_part #(.width(6)) comparator_35 (.a(in_1[5:0]), .b({6{1'b0}}), .eq(comparator_35_eq));  // open: gt, lt
  Comparator_part #(.width(6)) comparator_36 (.a(in_1[31:26]), .b(6'b111000), .eq(comparator_36_eq));  // open: gt, lt
  Comparator_part #(.width(6)) comparator_37 (.a(in_1[5:0]), .b(6'b000001), .eq(comparator_37_eq));  // open: gt, lt
  Comparator_part #(.width(6)) comparator_38 (.a(in_1[5:0]), .b(6'b001000), .eq(comparator_38_eq));  // open: gt, lt
  Comparator_part #(.width(6)) comparator_39 (.a(in_1[5:0]), .b(6'b010000), .eq(comparator_39_eq));  // open: gt, lt
  Comparator_part #(.width(6)) comparator_40 (.a(in_1[5:0]), .b(6'b010010), .eq(comparator_40_eq));  // open: gt, lt
  and and_18 (Output_33, comparator_34_eq, comparator_35_eq);
  and and_19 (Output_35, comparator_36_eq, comparator_37_eq);
  and and_20 (Output_37, _000000, comparator_38_eq);
  and and_21 (Output_39, _000000, comparator_39_eq);
  and and_22 (Output_41, _000000, comparator_40_eq);

  assign Output = in_1[25:21];
  assign Output_2 = in_1[25:0];
  assign Output_3 = in_1[20:16];
  assign Output_5 = in_1[15:0];
  assign Output_6 = in_1[15:11];

  // Other names for the same wires on the sheet: add = Output_11; addi = Output_9; and = Output_16; andi = Output_21;
  //   beq = Output_14; bgtz = Output_26; blez = Output_22; bltz = Output_30; bne = Output_18; div = Output_27;
  //   divu = Output_31; halt = Output_34; constant[15:0] = in_1[15:0]; dest[25:0] = in_1[25:0]; FC[5:0] = in_1[5:0];
  //   RD[4:0] = in_1[15:11]; RT[4:0] = in_1[20:16]; RS[4:0] = in_1[25:21]; OP[5:0] = in_1[31:26]; j = Output_4;
  //   jr = Output_37; kbd = Output_40; lw = Output_32; mfhi = Output_39; mflo = Output_41; mult = Output_19;
  //   mulu = Output_23; nop = Output_7; nor = Output_24; or = Output_20; ori = Output_25; pop = Output_33;
  //   push = Output_35; rnd = Output_38; slt = Output_8; slti = Output_13; sltiu = Output_17; sltu = Output_12;
  //   sub = Output_15; sw = Output_10; tty = Output_36; xor = Output_28; xori = Output_29

  // Notes on the sheet:
  //   IN
  //   Instrucciones Tipo I
  //   Instrucciones Tipo R
  //   OUT
  //   INSTRUCTION DECODER
  //   Instrucciones Tipo J
endmodule

module Instruction_Catcher (
  input  in_1,
  input  in_2,
  input  in_3,
  input  [31:0] in_4,
  output [31:0] Output
);

  Register #(.width(32)) register_1 (
    .D(in_4), .en(in_3), .Q({Output[7:0], Output[15:8], Output[23:16], Output[31:24]}), .clk(in_1), .clr(in_2));

  // Other names for the same wires on the sheet: clock = in_1; enable = in_3; instruction[31:0] = in_4; reset = in_2

  // Notes on the sheet:
  //   INSTRUCTION
  //   CATCHER
endmodule

module ALU (
  input  in_1,
  input  in_2,
  input  [31:0] Input,
  input  [31:0] Input_2,
  input  [3:0] in_5,
  output [31:0] Output,
  output [31:0] Output_2,
  output [31:0] Output_3
);

  wire div, enable, mult;
  wire [31:0] add, \and , div_rem, div_res, mult_high, mult_low, multiplexer_2_out, multiplexer_3_out,
       \nand , \nor , \or , slt, sub, \xor ;

  assign \and  = Input & Input_2;  // AND_Gate and_1, 32 bits wide
  assign \or  = Input | Input_2;  // OR_Gate or_1, 32 bits wide
  assign \nand  = ~(Input & Input_2);  // NAND_Gate nand_1, 32 bits wide
  assign \nor  = ~(Input | Input_2);  // NOR_Gate nor_1, 32 bits wide
  assign \xor  = Input ^ Input_2;  // XOR_Gate xor_1, 32 bits wide
  Adder #(.width(32)) adder_1 (.a(Input), .b(Input_2), .out(add));  // open: cin, cout
  Subtractor #(.width(32)) subtractor_1 (.a(Input), .b(Input_2), .out(sub));  // open: bin, bout
  Divider divider_1 (.in_1(Input), .in_2(in_1), .in_3(Input_2), .out_4(div_res), .out_5(div_rem));
  Multiplier multiplier_1 (.in_1(Input), .in_2(in_1), .in_3(Input_2), .Output(mult_high), .Output_2(mult_low));
  Comparator comparator_1 (.in_2(Input), .in_1(in_1), .in_3(Input_2), .Output(slt));
  Multiplexer #(.select(4), .width(32), .enable("false")) multiplexer_1 (
    .in0(add), .in1(sub), .in4(slt), .in5(\and ), .in6(\or ), .in7(\nor ), .in8(\xor ), .out(Output),
    .sel(in_5));  // open: in2, in3, in9, in10, in11, in12, in13, in14, in15
  and and_2 (mult, ~in_5[0], in_5[1], ~in_5[2], ~in_5[3]);  // AND_Gate
  and and_3 (div, in_5[0], in_5[1], ~in_5[2], ~in_5[3]);  // AND_Gate
  or or_2 (enable, mult, div);
  Multiplexer #(.width(32), .enable("false")) multiplexer_2 (
    .in0(mult_low), .in1(div_res), .out(multiplexer_2_out), .sel(div));
  Multiplexer #(.width(32), .enable("false")) multiplexer_3 (
    .in0(mult_high), .in1(div_rem), .out(multiplexer_3_out), .sel(div));
  Register #(.width(32)) register_1 (.D(multiplexer_2_out), .en(enable), .Q(Output_2), .clk(in_2));  // open: clr
  Register #(.width(32)) register_2 (.D(multiplexer_3_out), .en(enable), .Q(Output_3), .clk(in_2));  // open: clr

  // Other names for the same wires on the sheet: a[31:0] = Input; b[31:0] = Input_2; clock = in_2;
  //   HI[31:0] = Output_3; LO[31:0] = Output_2; _0 = in_5[0]; selector[3:0] = in_5; _1 = in_5[1]; _2 = in_5[2];
  //   _3 = in_5[3]; sign = in_1

  // Notes on the sheet:
  //   ALU
endmodule

module ALU_Encoder (
  input  in_1,
  input  in_2,
  input  in_3,
  input  in_4,
  input  in_5,
  input  in_6,
  input  in_7,
  input  in_8,
  input  in_9,
  input  in_10,
  input  in_11,
  input  in_12,
  input  in_13,
  input  in_14,
  input  in_15,
  input  in_16,
  input  in_17,
  input  in_18,
  output sign,
  output I,
  output [3:0] selector
);

  wire AND, DIV, MUL, OR, SLT, SLTI;

  or or_1 (MUL, in_3, in_4);
  or or_2 (DIV, in_5, in_6);
  or or_3 (SLT, in_7, in_8);
  or or_4 (SLTI, in_14, in_15);
  or or_5 (selector[0], in_2, DIV, AND, in_11);
  or or_6 (AND, in_9, in_16);
  or or_7 (OR, in_10, in_17);
  or or_8 (selector[3], in_12, in_18);
  or or_9 (selector[1], MUL, DIV, OR, in_11);
  or or_10 (selector[2], SLT, SLTI, OR, AND, in_11);
  or or_11 (sign, in_3, in_5, in_7, in_14);
  or or_12 (I, in_13, SLTI, in_16, in_17, in_18);

  // Other names for the same wires on the sheet: add = in_1; addi = in_13; and_t = in_9; andi = in_16; div_t = in_5;
  //   divu = in_6; mul_t = in_3; mulu = in_4; nor = in_11; or_t = in_10; ori = in_17; _0 = selector[0];
  //   _1 = selector[1]; _2 = selector[2]; _3 = selector[3]; XOR = selector[3]; slt_t = in_7; slti_t = in_14;
  //   sltiu = in_15; sltu = in_8; sub = in_2; xor_t = in_12; xori = in_18

  // Notes on the sheet:
  //   ALU ENCODER
endmodule

module Multiplier (
  input  [31:0] in_1,
  input  in_2,
  input  [31:0] in_3,
  output [31:0] Output,
  output [31:0] Output_2
);

  wire adder_1_cout, adder_3_cout, adder_5_cout, and_1_out, c1, c2, ca, cb;
  wire [31:0] a_2, a_cb, adder_1_out, adder_2_out, adder_3_out, adder_4_out, and_2_out, and_3_out, b_2, b_ca,
       bit_extender_1_out, bit_extender_2_out, c_ab, HI, HIU, LO, LOU, multiplier_2_cout, multiplier_2_out,
       shift_left_2_out_3, shift_left_3_out_3, shift_left_4_out_3, shift_left_out_3;

  SHR shr_1 (.in_1(in_1), .out_3(a_2), .Output(ca), .in_2(1'b0));
  and and_1 (and_1_out, ca, cb);
  assign bit_extender_1_out = {{31{cb}}, cb};  // Bit_Extender bit_extender_1
  assign bit_extender_2_out = {{31{ca}}, ca};  // Bit_Extender bit_extender_2
  assign c_ab = {{31{1'b0}}, and_1_out};  // Bit_Extender bit_extender_3
  SHR shr_2 (.in_1(in_3), .out_3(b_2), .Output(cb), .in_2(1'b0));
  assign and_2_out = a_2 & bit_extender_1_out;  // AND_Gate and_2, 32 bits wide
  assign and_3_out = b_2 & bit_extender_2_out;  // AND_Gate and_3, 32 bits wide
  Multiplier_part #(.width(32)) multiplier_1 (.a(in_1), .b(in_3), .out(LO), .cout(HI));  // open: cin
  SHL shl_1 (.in_1(and_2_out), .out_3(a_cb), .in_2(1'b0));  // open: Output
  SHL shl_2 (.in_1(and_3_out), .out_3(b_ca), .in_2(1'b0));  // open: Output
  Multiplier_part #(.width(32)) multiplier_2 (
    .a(a_2), .b(b_2), .out(multiplier_2_out), .cout(multiplier_2_cout));  // open: cin
  SHL shift_left (.in_1(multiplier_2_out), .out_3(shift_left_out_3), .Output(c1), .in_2(1'b0));
  SHL shift_left_2 (.in_1(multiplier_2_cout), .out_3(shift_left_2_out_3), .in_2(c1));  // open: Output
  SHL shift_left_3 (.in_1(shift_left_out_3), .out_3(shift_left_3_out_3), .Output(c2), .in_2(1'b0));
  // Probe on HIU
  SHL shift_left_4 (.in_1(shift_left_2_out_3), .out_3(shift_left_4_out_3), .in_2(c2));  // open: Output
  Multiplexer #(.width(32), .enable("false")) multiplexer_1 (.in0(HIU), .in1(HI), .out(Output), .sel(in_2));
  Multiplexer #(.width(32), .enable("false")) multiplexer_2 (.in0(LOU), .in1(LO), .out(Output_2), .sel(in_2));
  Adder #(.width(32)) adder_1 (.a(shift_left_3_out_3), .b(a_cb), .out(adder_1_out), .cout(adder_1_cout));  // open: cin
  Adder #(.width(32)) adder_2 (
    .a(shift_left_4_out_3), .b({32{1'b0}}), .out(adder_2_out), .cin(adder_1_cout));  // open: cout
  Adder #(.width(32)) adder_3 (.a(adder_1_out), .b(b_ca), .out(adder_3_out), .cout(adder_3_cout));  // open: cin
  Adder #(.width(32)) adder_4 (.a(adder_2_out), .b({32{1'b0}}), .out(adder_4_out), .cin(adder_3_cout));  // open: cout
  Adder #(.width(32)) adder_5 (.a(adder_3_out), .b(c_ab), .out(LOU), .cout(adder_5_cout));  // open: cin
  Adder #(.width(32)) adder_6 (.a(adder_4_out), .b({32{1'b0}}), .out(HIU), .cin(adder_5_cout));  // open: cout

  // Other names for the same wires on the sheet: a[31:0] = in_1; b[31:0] = in_3; sign = in_2

  // Notes on the sheet:
  //   MULTIPLIER
endmodule

module Divider (
  input  [31:0] in_1,
  input  in_2,
  input  [31:0] in_3,
  output [31:0] out_4,
  output [31:0] out_5
);

  wire neg_a, neg_b, neg_div, xor_2_out;
  wire [31:0] abs_a, abs_b, abs_div, adder_1_out, multiplexer_3_out, negator_1_out, negator_2_out,
       negator_3_out, negator_4_out, R, res, subtractor_1_out;

  and and_1 (neg_a, in_1[31], in_2);
  and and_2 (neg_b, in_2, in_3[31]);
  Negator #(.width(32)) negator_1 (.in(in_1), .out(negator_1_out));
  Negator #(.width(32)) negator_2 (.in(in_3), .out(negator_2_out));
  Multiplexer #(.width(32), .enable("false")) multiplexer_1 (.in0(in_1), .in1(negator_1_out), .out(abs_a), .sel(neg_a));
  Multiplexer #(.width(32), .enable("false")) multiplexer_2 (.in0(in_3), .in1(negator_2_out), .out(abs_b), .sel(neg_b));
  Divider_part #(.width(32)) divider_1 (.a(abs_a), .b(abs_b), .out(res), .rem(R));  // open: upper
  xor xor_1 (neg_div, neg_a, neg_b);
  Adder #(.width(32)) adder_1 (.a(res), .b(32'h1), .out(adder_1_out));  // open: cin, cout
  Multiplexer #(.width(32), .enable("false")) multiplexer_3 (
    .in0(res), .in1(adder_1_out), .out(multiplexer_3_out), .sel(neg_a));
  Negator #(.width(32)) negator_3 (.in(abs_div), .out(negator_3_out));
  Multiplexer #(.width(32), .enable("false")) multiplexer_4 (
    .in0(multiplexer_3_out), .in1(negator_4_out), .out(out_4), .sel(xor_2_out));
  Negator #(.width(32)) negator_4 (.in(multiplexer_3_out), .out(negator_4_out));
  xor xor_2 (xor_2_out, neg_a, neg_b);
  Multiplexer #(.width(32), .enable("false")) multiplexer_5 (
    .in0(abs_div), .in1(negator_3_out), .out(out_4), .sel(neg_div));
  Subtractor #(.width(32)) subtractor_1 (.a(abs_b), .b(R), .out(subtractor_1_out));  // open: bin, bout
  Multiplexer #(.width(32), .enable("false")) multiplexer_6 (.in0(R), .in1(subtractor_1_out), .out(out_5), .sel(neg_a));

  // Other names for the same wires on the sheet: a[31:0] = in_1; b[31:0] = in_3; div[31:0] = out_4;
  //   remainder[31:0] = out_5; sign = in_2

  // Notes on the sheet:
  //   DIVIDER
endmodule

module Comparator (
  input  in_1,
  input  [31:0] in_2,
  input  [31:0] in_3,
  output [31:0] Output
);

  wire multiplexer_1_out, slt, sltu;

  Comparator_part #(.width(32)) comparator_1 (.a(in_2), .b(in_3), .lt(slt));  // open: gt, eq
  Comparator_part #(.width(32), .mode("unsigned")) comparator_2 (.a(in_2), .b(in_3), .lt(sltu));  // open: gt, eq
  Multiplexer #(.enable("false")) multiplexer_1 (.in0(sltu), .in1(slt), .out(multiplexer_1_out), .sel(in_1));
  assign Output = {{31{1'b0}}, multiplexer_1_out};  // Bit_Extender bit_extender_1

  // Other names for the same wires on the sheet: a[31:0] = in_2; b[31:0] = in_3; sign = in_1

  // Notes on the sheet:
  //   COMPARATOR
endmodule

module SHR (
  input  [31:0] in_1,
  input  in_2,
  output [31:0] out_3,
  output Output
);


  assign out_3 = {in_2, in_1[31:1]};
  assign Output = in_1[0];

  // Other names for the same wires on the sheet: a[31:0] = in_1; a_2[31:0] = {in_2, in_1[31:1]}
endmodule

module SHL (
  input  [31:0] in_1,
  input  in_2,
  output [31:0] out_3,
  output Output
);


  assign out_3 = {in_1[30:0], in_2};
  assign Output = in_1[31];

  // Other names for the same wires on the sheet: a[31:0] = in_1; a_2[31:0] = {in_1[30:0], in_2}
endmodule

module Register_File (
  input  in_1,
  input  in_2,
  input  in_3,
  input  [31:0] in_4,
  input  in_5,
  input  in_6,
  input  in_7,
  input  [4:0] in_8,
  input  [4:0] in_9,
  input  [4:0] in_10,
  output [31:0] Output,
  output [31:0] Output_2,
  output [31:0] Output_3
);

  wire input31, L0, L1, L2, L3, L4, L5, L6, L7, L8, L9, L10, L11, L12, L13, L14, L15, L16, L17, L18, L19,
       L20, L21, L22, L23, L24, L25, L26, L27, L28, L29, L30, L31, or_1_out, or_2_out;
  wire [31:0] adder_1_out, multiplexer_3_out, multiplexer_4_out, out0, out1, out2, out3, out4, out5, out6,
       out7, out8, out9, out10, out11, out12, out13, out14, out15, out16, out17, out18, out19, out20, out21,
       out22, out23, out24, out25, out26, out27, out28, out29, out30, SP, subtractor_1_out;

  Demultiplexer #(.select(5), .enable("false")) demultiplexer_1 (
    .out0(L0), .out1(L1), .out2(L2), .out3(L3), .out4(L4), .out5(L5), .out6(L6), .out7(L7), .out8(L8),
    .out9(L9), .out10(L10), .out11(L11), .out12(L12), .out13(L13), .out14(L14), .out15(L15), .out16(L16),
    .out17(L17), .out18(L18), .out19(L19), .out20(L20), .out21(L21), .out22(L22), .out23(L23), .out24(L24),
    .out25(L25), .out26(L26), .out27(L27), .out28(L28), .out29(L29), .out30(L30), .out31(input31), .in(in_2),
    .sel(in_8));
  Register #(.width(32)) register_1 (.D({32{1'b0}}), .en(L0), .Q(out0), .clk(in_5), .clr(in_1));
  Register #(.width(32)) register_2 (.D(in_4), .en(L8), .Q(out8), .clk(in_5), .clr(in_1));
  Register #(.width(32)) register_3 (.D(in_4), .en(L16), .Q(out16), .clk(in_5), .clr(in_1));
  Register #(.width(32)) register_4 (.D(in_4), .en(L24), .Q(out24), .clk(in_5), .clr(in_1));
  Register #(.width(32)) register_5 (.D(in_4), .en(L1), .Q(out1), .clk(in_5), .clr(in_1));
  Register #(.width(32)) register_6 (.D(in_4), .en(L9), .Q(out9), .clk(in_5), .clr(in_1));
  Register #(.width(32)) register_7 (.D(in_4), .en(L17), .Q(out17), .clk(in_5), .clr(in_1));
  Register #(.width(32)) register_8 (.D(in_4), .en(L25), .Q(out25), .clk(in_5), .clr(in_1));
  Multiplexer #(.select(5), .width(32), .enable("false")) multiplexer_1 (
    .in0(out0), .in1(out1), .in2(out2), .in3(out3), .in4(out4), .in5(out5), .in6(out6), .in7(out7),
    .in8(out8), .in9(out9), .in10(out10), .in11(out11), .in12(out12), .in13(out13), .in14(out14),
    .in15(out15), .in16(out16), .in17(out17), .in18(out18), .in19(out19), .in20(out20), .in21(out21),
    .in22(out22), .in23(out23), .in24(out24), .in25(out25), .in26(out26), .in27(out27), .in28(out28),
    .in29(out29), .in30(out30), .in31(Output_3), .out(Output), .sel(in_9));
  Register #(.width(32)) register_9 (.D(in_4), .en(L2), .Q(out2), .clk(in_5), .clr(in_1));
  Register #(.width(32)) register_10 (.D(in_4), .en(L10), .Q(out10), .clk(in_5), .clr(in_1));
  Register #(.width(32)) register_11 (.D(in_4), .en(L18), .Q(out18), .clk(in_5), .clr(in_1));
  Register #(.width(32)) register_12 (.D(in_4), .en(L26), .Q(out26), .clk(in_5), .clr(in_1));
  Multiplexer #(.select(5), .width(32), .enable("false")) multiplexer_2 (
    .in0(out0), .in1(out1), .in2(out2), .in3(out3), .in4(out4), .in5(out5), .in6(out6), .in7(out7),
    .in8(out8), .in9(out9), .in10(out10), .in11(out11), .in12(out12), .in13(out13), .in14(out14),
    .in15(out15), .in16(out16), .in17(out17), .in18(out18), .in19(out19), .in20(out20), .in21(out21),
    .in22(out22), .in23(out23), .in24(out24), .in25(out25), .in26(out26), .in27(out27), .in28(out28),
    .in29(out29), .in30(out30), .in31(Output_3), .out(Output_2), .sel(in_10));
  Register #(.width(32)) register_13 (.D(in_4), .en(L3), .Q(out3), .clk(in_5), .clr(in_1));
  Register #(.width(32)) register_14 (.D(in_4), .en(L11), .Q(out11), .clk(in_5), .clr(in_1));
  Register #(.width(32)) register_15 (.D(in_4), .en(L19), .Q(out19), .clk(in_5), .clr(in_1));
  Register #(.width(32)) register_16 (.D(in_4), .en(L27), .Q(out27), .clk(in_5), .clr(in_1));
  Register #(.width(32)) register_17 (.D(in_4), .en(L4), .Q(out4), .clk(in_5), .clr(in_1));
  Register #(.width(32)) register_18 (.D(in_4), .en(L12), .Q(out12), .clk(in_5), .clr(in_1));
  Register #(.width(32)) register_19 (.D(in_4), .en(L20), .Q(out20), .clk(in_5), .clr(in_1));
  Register #(.width(32)) register_20 (.D(in_4), .en(L28), .Q(out28), .clk(in_5), .clr(in_1));
  Register #(.width(32)) register_21 (.D(in_4), .en(L5), .Q(out5), .clk(in_5), .clr(in_1));
  Register #(.width(32)) register_22 (.D(in_4), .en(L13), .Q(out13), .clk(in_5), .clr(in_1));
  Register #(.width(32)) register_23 (.D(in_4), .en(L21), .Q(out21), .clk(in_5), .clr(in_1));
  Register #(.width(32)) register_24 (.D(in_4), .en(L29), .Q(out29), .clk(in_5), .clr(in_1));
  or or_1 (or_1_out, in_3, in_7);
  Register #(.width(32)) register_25 (.D(in_4), .en(L6), .Q(out6), .clk(in_5), .clr(in_1));
  Register #(.width(32)) register_26 (.D(in_4), .en(L14), .Q(out14), .clk(in_5), .clr(in_1));
  Register #(.width(32)) register_27 (.D(in_4), .en(L22), .Q(out22), .clk(in_5), .clr(in_1));
  Register #(.width(32)) register_28 (.D(in_4), .en(L30), .Q(out30), .clk(in_5), .clr(in_1));
  and and_1 (L31, in_6, or_1_out);
  Subtractor #(.width(32)) subtractor_1 (.a(Output_3), .b(32'h4), .out(subtractor_1_out));  // open: bin, bout
  Adder #(.width(32)) adder_1 (.a(32'h4), .b(Output_3), .out(adder_1_out));  // open: cin, cout
  Multiplexer #(.width(32), .enable("false")) multiplexer_3 (
    .in0(subtractor_1_out), .in1(adder_1_out), .out(multiplexer_3_out), .sel(in_7));
  Register #(.width(32)) register_29 (.D(in_4), .en(L7), .Q(out7), .clk(in_5), .clr(in_1));
  Register #(.width(32)) register_30 (.D(in_4), .en(L15), .Q(out15), .clk(in_5), .clr(in_1));
  Register #(.width(32)) register_31 (.D(in_4), .en(L23), .Q(out23), .clk(in_5), .clr(in_1));
  Multiplexer #(.width(32), .enable("false")) multiplexer_4 (
    .in0(SP), .in1(in_4), .out(multiplexer_4_out), .sel(input31));
  or or_2 (or_2_out, L31, input31, in_1);
  Multiplexer #(.width(32), .enable("false")) multiplexer_5 (
    .in0(multiplexer_3_out), .in1({32{1'b1}}), .out(SP), .sel(in_1));
  Register #(.width(32)) register_32 (.D(multiplexer_4_out), .en(or_2_out), .Q(Output_3), .clk(in_5));  // open: clr

  // Other names for the same wires on the sheet: A[31:0] = Output; B[31:0] = Output_2; clock = in_5;
  //   input[31:0] = in_4; memR_W = in_6; out31[31:0] = Output_3; outA[4:0] = in_9; outB[4:0] = in_10; pop = in_7;
  //   push = in_3; reset = in_1; select[4:0] = in_8; write = in_2

  // Notes on the sheet:
  //   REGISTER FILE
endmodule

module Register_File_Input (
  input  [6:0] in_1,
  input  [31:0] in_2,
  input  in_3,
  input  in_4,
  input  [31:0] in_5,
  input  in_6,
  input  in_7,
  input  [31:0] in_8,
  input  in_9,
  input  in_10,
  input  [31:0] in_11,
  input  [31:0] in_12,
  output [31:0] Output
);

  wire [2:0] selector;

  or or_1 (selector[0], in_3, in_4, in_7, in_10);
  or or_2 (selector[1], in_6, in_7);
  or or_3 (selector[2], in_9, in_10);
  Multiplexer #(.select(3), .width(32), .enable("false")) multiplexer_1 (
    .in0(in_2), .in1(in_8), .in2(in_11), .in3(in_12), .in4(in_5), .in5({{25{1'b0}}, in_1}), .out(Output),
    .sel(selector));  // open: in6, in7

  // Other names for the same wires on the sheet: ALU[31:0] = in_2; HI[31:0] = in_11; is_kbd = in_10; is_rnd = in_9;
  //   KBD[6:0] = in_1; LO[31:0] = in_12; lw = in_3; memoryA[31:0] = in_8; mfhi = in_6; mflo = in_7; pop = in_4;
  //   RND[31:0] = in_5

  // Notes on the sheet:
  //   REGISTER FILE INPUT
endmodule

module Memory_Address (
  input  [31:0] in_1,
  input  [31:0] in_2,
  input  [31:0] in_3,
  input  in_4,
  input  in_5,
  input  in_6,
  input  in_7,
  input  in_8,
  output [31:0] Output
);

  wire [1:0] or_2_out;
  wire [31:0] multiplexer_1_out, subtractor_1_out;

  Subtractor #(.width(32)) subtractor_1 (.a(in_3), .b(32'h4), .out(subtractor_1_out));  // open: bin, bout
  Multiplexer #(.width(32), .enable("false")) multiplexer_1 (
    .in0(in_3), .in1(subtractor_1_out), .out(multiplexer_1_out), .sel(in_7));
  or or_1 (or_2_out[1], in_6, in_8, in_7);
  Multiplexer #(.select(2), .width(32), .enable("false")) multiplexer_2 (
    .in0(in_1), .in1(in_2), .in2(multiplexer_1_out), .in3(in_1), .out(Output), .sel(or_2_out));
  or or_2 (or_2_out[0], in_4, in_8, in_5);

  // Other names for the same wires on the sheet: ALU[31:0] = in_2; isPC = in_8; lw = in_4; PC[31:0] = in_1;
  //   pop = in_6; push = in_7; SP[31:0] = in_3; sw = in_5

  // Notes on the sheet:
  //   MEMORY ADDRESS
endmodule

module Program_Counter (
  input  in_1,
  input  in_2,
  input  in_3,
  input  [31:0] Input,
  output [31:0] Output
);

  Register #(.width(32)) register_1 (.D(Input), .en(in_2), .Q(Output), .clk(in_1), .clr(in_3));

  // Other names for the same wires on the sheet: clock = in_1; enable = in_2; reset = in_3

  // Notes on the sheet:
  //    COUNTER
  //   PROGRAM 
endmodule

module Branch_Control (
  input  [25:0] in_1,
  input  [31:0] in_2,
  input  [31:0] in_3,
  input  [31:0] in_4,
  input  [15:0] in_5,
  input  in_6,
  input  in_7,
  input  in_8,
  input  in_9,
  input  in_10,
  input  in_11,
  input  in_12,
  output [31:0] Output
);

  wire and_1_out, and_2_out, and_3_out, and_4_out, and_5_out, comparator_1_eq, or_2_out, RS_0, RS__0, RS__RT;
  wire [1:0] or_3_out;
  wire [13:0] bit_extender_1_out;
  wire [31:0] PC_4, PC_4_const;

  Comparator_part #(.width(32)) comparator_1 (.a(in_2), .b({32{1'b0}}), .eq(comparator_1_eq), .lt(RS_0));  // open: gt
  Comparator_part #(.width(32)) comparator_2 (.a(in_2), .b(in_3), .eq(RS__RT));  // open: gt, lt
  Adder #(.width(32)) adder_1 (.a(in_4), .b(32'h4), .out(PC_4));  // open: cin, cout
  assign bit_extender_1_out = {{13{in_5[15]}}, in_5[15]};  // Bit_Extender bit_extender_1
  or or_1 (RS__0, comparator_1_eq, RS_0);
  Adder #(.width(32)) adder_2 (.a(PC_4), .b({bit_extender_1_out, in_5, 2'b00}), .out(PC_4_const));  // open: cin, cout
  and and_1 (and_1_out, in_6, RS__RT);
  and and_2 (and_2_out, ~RS__RT, in_7);  // AND_Gate
  and and_3 (and_3_out, in_8, RS__0);
  and and_4 (and_4_out, ~RS__0, in_9);  // AND_Gate
  and and_5 (and_5_out, RS_0, in_10);
  or or_2 (or_2_out, and_1_out, and_2_out, and_3_out, and_4_out, and_5_out);
  or or_3 (or_3_out[0], or_2_out, in_11);
  or or_4 (or_3_out[1], in_11, in_12);
  Multiplexer #(.select(2), .width(32), .enable("false")) multiplexer_1 (
    .in0(PC_4), .in1(PC_4_const), .in2({in_4[31:28], in_1, 2'b00}), .in3(in_2), .out(Output), .sel(or_3_out));

  // Other names for the same wires on the sheet: const[15:0] = in_5; beq = in_6; bgtz = in_9; blez = in_8;
  //   bltz = in_10; bne = in_7; j = in_12; dest[25:0] = in_1; jmp[31:2] = {in_4[31:28], in_1}; jr = in_11;
  //   PC[31:0] = in_4; RS[31:0] = in_2; RT[31:0] = in_3

  // Notes on the sheet:
  //   BRANCH CONTROL
endmodule

module RAM_Interaction (
  input  [31:0] in_1,
  input  [31:0] in_2,
  input  [31:0] in_3,
  input  [31:0] in_4,
  input  [31:0] in_5,
  input  [3:0] in_6,
  input  [3:0] in_7,
  input  in_8,
  input  in_9,
  input  in_10,
  input  in_11,
  input  in_12,
  input  in_13,
  output [31:0] Output,
  output [31:0] Output_2,
  output [31:0] Output_3,
  output [31:0] Output_4,
  output [15:0] Output_5,
  output [3:0] Output_6,
  output Output_7,
  output Output_8,
  output Output_9,
  output Output_10,
  output Output_11
);

  wire CSD, CSI, or_1_out, stop;
  wire [31:0] DO0, DO1, DO2, DO3, IO0, IO1, IO2, IO3;

  D_Flip_Flop #(.trigger("falling")) d_ff_1 (
    .clk(in_8), .D(in_10), .Q(Output_8), .en(or_1_out));  // open: Qn, preset, reset
  or or_1 (or_1_out, in_10, stop);
  RAM_Reader ram_reader_1 (
    .in_1(in_1), .in_2(in_2), .in_3(in_3), .in_4(in_4), .in_5(in_6), .in_7(in_9), .in_8(in_11), .Output(IO0),
    .Output_2(IO1), .Output_3(IO2), .Output_4(IO3), .Output_5(CSI), .Output_6(Output_9), .in_6(in_8));
  Multiplexer #(.width(32), .enable("false")) multiplexer_1 (
    .in0({DO0[7:0], DO0[15:8], DO0[23:16], DO0[31:24]}), .in1(IO0), .out(Output), .sel(in_13));
  Timer timer_1 (.in_1(Output_8), .in_2(Output_11), .in_3(in_8), .in_4(in_7), .Output(stop));
  D_Flip_Flop #(.trigger("falling")) d_ff_2 (.clk(in_8), .D(stop), .Q(Output_11));  // open: Qn, preset, en, reset
  RAM_Reader ram_reader_2 (
    .in_1(in_1), .in_2(in_2), .in_3(in_3), .in_4(in_4), .in_5(in_6), .in_7(in_9), .in_8(in_12), .Output(DO0),
    .Output_2(DO1), .Output_3(DO2), .Output_4(DO3), .Output_5(CSD), .Output_6(Output_10), .in_6(in_8));
  Multiplexer #(.width(32), .enable("false")) multiplexer_2 (
    .in0({DO1[7:0], DO1[15:8], DO1[23:16], DO1[31:24]}), .in1(IO1), .out(Output_2), .sel(in_13));
  Multiplexer #(.width(32), .enable("false")) multiplexer_3 (
    .in0({DO2[7:0], DO2[15:8], DO2[23:16], DO2[31:24]}), .in1(IO2), .out(Output_3), .sel(in_13));
  Demultiplexer #(.select(2), .enable("false")) demultiplexer_1 (
    .out0(Output_6[0]), .out1(Output_6[1]), .out2(Output_6[2]), .out3(Output_6[3]), .in(1'b1), .sel(in_5[3:2]));
  or or_2 (Output_7, CSD, CSI, Output_8);
  Multiplexer #(.width(32), .enable("false")) multiplexer_4 (
    .in0({DO3[7:0], DO3[15:8], DO3[23:16], DO3[31:24]}), .in1(IO3), .out(Output_4), .sel(in_13));

  assign Output_5 = in_5[19:4];

  // Other names for the same wires on the sheet: bank0[31:0] = in_1; bank1[31:0] = in_2; bank2[31:0] = in_3;
  //   bank3[31:0] = in_4; clock = in_8; CS = Output_7; DP_address[31:0] = in_5; address[15:0] = in_5[19:4];
  //   get_data = in_12; get_inst = in_11; is_inst = in_13; mask[3:0] = Output_6; out_bank0[31:0] = Output;
  //   out_bank1[31:0] = Output_2; out_bank2[31:0] = Output_3; out_bank3[31:0] = Output_4; read_time[3:0] = in_6;
  //   ready_data = Output_10; ready_inst = Output_9; ready_write = Output_11; reset = in_9; RW = Output_8;
  //   write = in_10; write_time[3:0] = in_7

  // Notes on the sheet:
  //   RAM INTERACTOR
endmodule

module RAM_Reader (
  input  [31:0] in_1,
  input  [31:0] in_2,
  input  [31:0] in_3,
  input  [31:0] in_4,
  input  [3:0] in_5,
  input  in_6,
  input  in_7,
  input  in_8,
  output [31:0] Output,
  output [31:0] Output_2,
  output [31:0] Output_3,
  output [31:0] Output_4,
  output Output_5,
  output Output_6
);

  wire a, enable, or_1_out, stop;

  D_Flip_Flop #(.trigger("falling")) d_ff_1 (.clk(in_6), .D(in_8), .Q(a), .en(or_1_out));  // open: Qn, preset, reset
  or or_1 (or_1_out, in_8, stop);
  Register #(.width(32)) register_1 (.D(in_1), .en(enable), .Q(Output), .clk(in_6), .clr(in_7));
  Timer timer_1 (.in_1(a), .in_2(Output_6), .in_3(in_6), .in_4(in_5), .Output(stop));
  Register #(.width(32)) register_2 (.D(in_2), .en(enable), .Q(Output_2), .clk(in_6), .clr(in_7));
  D_Flip_Flop #(.trigger("falling")) d_ff_2 (
    .clk(in_6), .D(stop), .Q(enable), .reset(Output_6));  // open: Qn, preset, en
  D_Flip_Flop #(.trigger("falling")) d_ff_3 (.clk(in_6), .D(enable), .Q(Output_6));  // open: Qn, preset, en, reset
  Register #(.width(32)) register_3 (.D(in_3), .en(enable), .Q(Output_3), .clk(in_6), .clr(in_7));
  or or_2 (Output_5, a, enable);
  Register #(.width(32)) register_4 (.D(in_4), .en(enable), .Q(Output_4), .clk(in_6), .clr(in_7));

  // Other names for the same wires on the sheet: bank0[31:0] = in_1; bank1[31:0] = in_2; bank2[31:0] = in_3;
  //   bank3[31:0] = in_4; clock = in_6; CS = Output_5; get = in_8; out_bank0[31:0] = Output;
  //   out_bank1[31:0] = Output_2; out_bank2[31:0] = Output_3; out_bank3[31:0] = Output_4; read_time[3:0] = in_5;
  //   ready = Output_6; reset = in_7

  // Notes on the sheet:
  //   RAM READER
endmodule

module Timer (
  input  in_1,
  input  in_2,
  input  in_3,
  input  [3:0] in_4,
  output Output
);

  wire [3:0] counter_1_q;

  Counter #(.width(4), .max('hf)) counter_1 (
    .count(in_1), .Q(counter_1_q), .clk(in_3), .clr(in_2));  // open: load, D, carry
  Comparator_part #(.width(4)) comparator_1 (.a(in_4), .b(counter_1_q), .eq(Output));  // open: gt, lt

  // Other names for the same wires on the sheet: clock = in_3; ready = Output; reset = in_2; start = in_1;
  //   wait_time[3:0] = in_4

  // Notes on the sheet:
  //   TIMER
endmodule
